// Logisim project LAB2_AADR_2306152374_AhmadDzulfikarAsShavy.circ as structural Verilog: 2 circuits, main circuit SOP
module SOP (
  input  A,
  input  B,
  input  C,
  input  D,
  output O
);

  wire and_1_out, and_2_out, and_3_out, and_4_out, not_1_out, not_2_out, not_3_out, or_1_out;

  not not_1 (not_1_out, A);
  not not_2 (not_2_out, C);
  and and_1 (and_1_out, not_1_out, B);
  and and_2 (and_2_out, and_1_out, not_2_out);
  not not_3 (not_3_out, D);
  and and_3 (and_3_out, B, A);
  or or_1 (or_1_out, and_2_out, not_3_out);
  and and_4 (and_4_out, and_3_out, C);
  or or_2 (O, and_4_out, or_1_out);
endmodule

module POS (
  input  A,
  input  B,
  input  C,
  input  D,
  output O
);

  wire and_1_out, not_1_out, not_2_out, not_3_out, or_1_out, or_2_out, or_3_out, or_4_out, or_5_out;

  not not_1 (not_1_out, D);
  not not_2 (not_2_out, A);
  or or_1 (or_1_out, not_2_out, C);
  not not_3 (not_3_out, C);
  or or_2 (or_2_out, B, not_1_out);
  or or_3 (or_3_out, or_1_out, not_1_out);
  or or_4 (or_4_out, A, not_3_out);
  or or_5 (or_5_out, or_4_out, not_1_out);
  and and_1 (and_1_out, or_2_out, or_3_out);
  and and_2 (O, or_5_out, and_1_out);
endmodule
