// Logisim project LAB3_AADR_2306152374_AhmadDzulfikarAsShavy.circ as structural Verilog: 3 circuits, main circuit ORGate
module ORGate (
  input  x,
  input  y,
  output xy
);

  wire nor_1_out;

  nor nor_1 (nor_1_out, x, y);
  nor nor_2 (xy, nor_1_out, nor_1_out);
endmodule

module ANDGate (
  input  x,
  input  y,
  output xy
);

  wire nor_1_out, nor_2_out;

  nor nor_1 (nor_1_out, x, x);
  nor nor_2 (nor_2_out, y, y);
  nor nor_3 (xy, nor_1_out, nor_2_out);
endmodule

module Code_Converter (
  input  A,
  input  B,
  input  C,
  input  D,
  output W,
  output X,
  output Y,
  output Z
);

  wire andgate_1_xy, andgate_2_xy, andgate_3_xy, andgate_4_xy, andgate_5_xy, andgate_6_xy, andgate_7_xy,
       nor_1_out, nor_2_out, orgate_1_xy, orgate_2_xy;

  nor nor_1 (nor_1_out, B, B);
  nor nor_2 (nor_2_out, C, C);
  nor nor_3 (Z, D, D);
  ANDGate andgate_1 (.x(C), .y(D), .xy(andgate_1_xy));
  ANDGate andgate_2 (.x(B), .y(C), .xy(andgate_2_xy));
  ANDGate andgate_3 (.x(andgate_2_xy), .y(D), .xy(andgate_3_xy));
  ANDGate andgate_4 (.x(nor_1_out), .y(nor_2_out), .xy(andgate_4_xy));
  ANDGate andgate_5 (.x(nor_1_out), .y(Z), .xy(andgate_5_xy));
  ANDGate andgate_6 (.x(Z), .y(C), .xy(andgate_6_xy));
  ANDGate andgate_7 (.x(nor_2_out), .y(D), .xy(andgate_7_xy));
  ORGate orgate_1 (.x(A), .y(B), .xy(orgate_1_xy));
  ORGate orgate_2 (.x(andgate_3_xy), .y(andgate_4_xy), .xy(orgate_2_xy));
  ORGate orgate_3 (.x(andgate_6_xy), .y(andgate_7_xy), .xy(Y));
  ORGate orgate_4 (.x(orgate_1_xy), .y(andgate_1_xy), .xy(W));
  ORGate orgate_5 (.x(orgate_2_xy), .y(andgate_5_xy), .xy(X));

  // Notes on the sheet:
  //   B'
  //   C'
  //   D'
  //   CD
  //   BC
  //   CD'
  //   C'D
  //   BCD
  //   B'C'
  //   B'D'
  //   A+B
  //   BCD+B'C'
  //   CD' + C'D
  //   A+B+CD
  //   BCD + B'C' + B'D'
endmodule
