// Logisim project Template_Lab_4 (1).circ as structural Verilog: 6 circuits, main circuit ParAdder
module main (
  input  [3:0] X,
  input  [3:0] Y,
  input  [1:0] A,
  output [3:0] R
);

  ParAdder paradder_1 (.Z(1'b0));  // open: X, Y, S
  OneComp onecomp_1 ();  // open: X, Y
  FourOneMul fouronemul_1 (.A(A), .R(R));  // open: D0, D1, D2

  // Notes on the sheet:
  //   X + Y
  //   1's Complement Converter
  //   What about 2's Complement?
endmodule

module FullAdder (
  input  X,
  input  Y,
  input  Z,
  output S,
  output C
);
endmodule

module ParAdder (
  input  [3:0] X,
  input  [3:0] Y,
  input  Z,
  output [3:0] S
);
endmodule

module OneComp (
  input  [3:0] X,
  output [3:0] Y
);
endmodule

module TwoFourDec (
  input  A0,
  input  A1,
  output D0,
  output D1,
  output D2,
  output D3
);
endmodule

module FourOneMul (
  input  [3:0] D0,
  input  [3:0] D1,
  input  [3:0] D2,
  input  [1:0] A,
  output [3:0] R
);

  wire twofourdec_1_d0, twofourdec_1_d1, twofourdec_1_d2;
  wire [3:0] and_1_out, and_2_out, and_3_out, bit_extender_1_out, bit_extender_2_out, bit_extender_3_out;

  TwoFourDec twofourdec_1 (
    .A0(A[0]), .A1(A[1]), .D0(twofourdec_1_d0), .D1(twofourdec_1_d1), .D2(twofourdec_1_d2));  // open: D3
  assign bit_extender_1_out = {{3{twofourdec_1_d0}}, twofourdec_1_d0};  // Bit_Extender bit_extender_1
  assign bit_extender_2_out = {{3{twofourdec_1_d1}}, twofourdec_1_d1};  // Bit_Extender bit_extender_2
  assign bit_extender_3_out = {{3{twofourdec_1_d2}}, twofourdec_1_d2};  // Bit_Extender bit_extender_3
  assign and_1_out = bit_extender_1_out & D0;  // AND_Gate and_1, 4 bits wide
  assign and_2_out = bit_extender_2_out & D1;  // AND_Gate and_2, 4 bits wide
  assign and_3_out = bit_extender_3_out & D2;  // AND_Gate and_3, 4 bits wide
  assign R = and_1_out | and_2_out | and_3_out;  // OR_Gate or_1, 4 bits wide

  // Notes on the sheet:
  //   4-Bit 4-to-1 Multiplexer
  //   Don't make any changes to this circuit!
  //   Bit extender from 1 bit to 4 bits
endmodule
