// Logisim project tm4.circ as structural Verilog
module twoToFour (
  input  A1,
  input  A0,
  output out_3,
  output out_4,
  output out_5,
  output out_6
);

  wire not_1_out, not_2_out;

  not not_1 (not_1_out, A1);
  not not_2 (not_2_out, A0);
  and and_1 (out_3, not_2_out, not_1_out);
  and and_2 (out_4, A0, not_1_out);
  and and_3 (out_5, not_2_out, A1);
  and and_4 (out_6, A0, A1);
endmodule

module fourToSixteen (
  input  in_1,
  input  in_2,
  input  in_3,
  input  in_4,
  output out_5,
  output out_6,
  output out_7,
  output out_8,
  output out_9,
  output out_10,
  output out_11,
  output out_12,
  output out_13,
  output out_14,
  output out_15,
  output out_16,
  output out_17,
  output out_18,
  output out_19,
  output out_20
);

  wire twotofour_1_out_3, twotofour_1_out_4, twotofour_1_out_5, twotofour_1_out_6, twotofour_2_out_3,
       twotofour_2_out_4, twotofour_2_out_5, twotofour_2_out_6;

  twoToFour twotofour_1 (
    .A1(in_1), .A0(in_2), .out_3(twotofour_1_out_3), .out_4(twotofour_1_out_4), .out_5(twotofour_1_out_5),
    .out_6(twotofour_1_out_6));
  twoToFour twotofour_2 (
    .A1(in_3), .A0(in_4), .out_3(twotofour_2_out_3), .out_4(twotofour_2_out_4), .out_5(twotofour_2_out_5),
    .out_6(twotofour_2_out_6));
  and and_1 (out_5, twotofour_1_out_3, twotofour_2_out_3);
  and and_2 (out_6, twotofour_1_out_3, twotofour_2_out_4);
  and and_3 (out_7, twotofour_1_out_3, twotofour_2_out_5);
  and and_4 (out_8, twotofour_1_out_3, twotofour_2_out_6);
  and and_5 (out_9, twotofour_1_out_4, twotofour_2_out_3);
  and and_6 (out_10, twotofour_1_out_4, twotofour_2_out_4);
  and and_7 (out_11, twotofour_1_out_4, twotofour_2_out_5);
  and and_8 (out_12, twotofour_1_out_4, twotofour_2_out_6);
  and and_9 (out_13, twotofour_1_out_5, twotofour_2_out_3);
  and and_10 (out_14, twotofour_1_out_5, twotofour_2_out_4);
  and and_11 (out_15, twotofour_1_out_5, twotofour_2_out_5);
  and and_12 (out_16, twotofour_1_out_5, twotofour_2_out_6);
  and and_13 (out_17, twotofour_1_out_6, twotofour_2_out_3);
  and and_14 (out_18, twotofour_1_out_6, twotofour_2_out_4);
  and and_15 (out_19, twotofour_1_out_6, twotofour_2_out_5);
  and and_16 (out_20, twotofour_1_out_6, twotofour_2_out_6);
endmodule
